# Fritzing sketch 2_led_toggle (saved by Fritzing 0.8.7b)
breadboards: 1

parts:
  IC1 = atmega328p [part_number=atmega328P package=dil28-3-simon-kit]  # not connected
  LED1 = LED - 5mm [color="Red (633nm)" package="5 mm [THT]"]
  C1 = Ceramic Capacitor [capacitance=100nF package="1206 [SMD, multilayer]"]  # not connected
  R1 = Resistor [tolerance=±5% resistance=220 package=THT]
  S1 = Pushbutton [package="[THT]"]
  LED2 = LED - 5mm [color="Red (633nm)" package="5 mm [THT]"]
  R2 = Resistor [tolerance=±5% resistance=220 package=THT]

nets:
  N1: LED1.cathode, R1.Pin_0
  N2: R1.Pin_1, S1.Pin_3, S1.Pin_4, R2.Pin_1
  N3: S1.Pin_1, S1.Pin_2
  N4: LED2.anode, R2.Pin_0

custom parts:
  atmega328p: MICROCONTROLLER 8 Kbytes FLASH 1 kbytes SRAM 512 bytes EEPROM USART 4-channel 10 bit ADC 2-channel 8 bit ADC
