# Fritzing sketch 6_led_with_button_and_ldr_and_pot (saved by Fritzing 0.9.0b)
breadboards: 1

parts:
  IC1 = atmega328p [part_number=atmega328P package=dil28-3-simon-kit]  # not connected
  C1 = Ceramic Capacitor [capacitance=100nF package="1206 [SMD, multilayer]"]  # not connected
  S1 = Pushbutton [package="[THT]"]
  LED3 = LED - 5mm [color="Red (633nm)" package="5 mm [THT]"]
  LED4 = LED - 5mm [color="Red (633nm)" package="5 mm [THT]"]
  LED5 = LED - 5mm [color="Red (633nm)" package="5 mm [THT]"]
  LED6 = LED - 5mm [color="Red (633nm)" package="5 mm [THT]"]
  R3 = Resistor [tolerance=±5% resistance=220 package=THT]
  R4 = Resistor [tolerance=±5% resistance=220 package=THT]
  R5 = Resistor [tolerance=±5% resistance=220 package=THT]
  R6 = Resistor [tolerance=±5% resistance=220 package=THT]
  LED7 = LED - 5mm [color="Red (633nm)" package="5 mm [THT]"]
  R7 = Resistor [tolerance=±5% resistance=220 package=THT]
  R8 = PHOTOCELL [package=photocell-kit]
  R9 = Resistor [tolerance=±5% resistance=220 package=THT]  # not connected
  R10 = Resistor [tolerance=±5% resistance=220 package=THT]  # not connected
  R11 = Resistor [tolerance=±5% resistance=220 package=THT]
  R12 = Rotary Potentiometer (Small) [maximum_resistance=100kΩ package=THT]

nets:
  N1: S1.Pin_1, S1.Pin_2
  N2: S1.Pin_3, S1.Pin_4, R3.Pin_1, R4.Pin_1, R5.Pin_1, R6.Pin_1, R7.Pin_1, R12.leg2
  N3: LED3.cathode, R3.Pin_0
  N4: LED4.cathode, R4.Pin_0
  N5: LED5.cathode, R5.Pin_0
  N6: LED6.cathode, R6.Pin_0
  N7: LED7.cathode, R7.Pin_0
  N8: R8.P$1, R11.Pin_0
  N9: R8.P$2, R12.leg1

custom parts:
  atmega328p: MICROCONTROLLER 8 Kbytes FLASH 1 kbytes SRAM 512 bytes EEPROM USART 4-channel 10 bit ADC 2-channel 8 bit ADC
